# Fritzing sketch RPI2040_iCue_Controller (saved by Fritzing 1.0.3b)
circuit board: 8.4cm x 3.1cm
breadboards: 1

parts:
  XIAO_RP2040 = seeeduino-xiao
  D1 = Schottky Diode [part_number=1N5817 package="300 mil [THT]"]
  R1 = Resistor [tolerance=±5% power=0.25W resistance=10k package=THT]
  LDR = Photocell (LDR) [power=0.25W dark_resistance_@0.01lx=300kΩ light_resistance_@100lx=400Ω luminance=10lx package=THT]
  R3 = Resistor [tolerance=±5% power=0.25W resistance=100 package=THT]
  R4 = Resistor [tolerance=±5% power=0.25W resistance=100 package=THT]
  R5 = Resistor [tolerance=±5% power=0.25W resistance=100 package=THT]
  R6 = Resistor [tolerance=±5% power=0.25W resistance=100 package=THT]
  R7 = Resistor [tolerance=±5% power=0.25W resistance=100 package=THT]
  R8 = Resistor [tolerance=±5% power=0.25W resistance=100 package=THT]
  R9 = Resistor [tolerance=±5% power=0.25W resistance=100 package=THT]
  R10 = Resistor [tolerance=±5% power=0.25W resistance=100 package=THT]
  PWR_5V = Screw terminal - 2 pins [package=THT]
  IC1 = Voltage Regulator LM1117 [package=sot223]
  DSP_OLED = OLED Mono 0.56 inch blue or white
  C1 = Ceramic Capacitor [capacitance=100nF voltage=35V package="100 mil [THT, multilayer]"]
  C2 = Ceramic Capacitor [capacitance=100nF voltage=35V package="100 mil [THT, multilayer]"]
  part = Pad [width=6.406163512702532 height=2.6448148380132133 connect=center]
  LEDCPU = male pin header, 4 pins [form="♂ (male)"]
  LEDFAN2 = male pin header, 4 pins [form="♂ (male)"]
  ICUE1 = male pin header, 4 pins [form="♂ (male)"]
  LEDFAN1 = male pin header, 4 pins [form="♂ (male)"]
  LEDFAN3 = male pin header, 4 pins [form="♂ (male)"]
  LEDEXTRA = male pin header, 4 pins [form="♂ (male)"]
  LEDAIO = male pin header, 4 pins [form="♂ (male)"]
  ICUE2 = male pin header, 4 pins [form="♂ (male)"]

nets:
  N1: XIAO_RP2040.D0, R1.Pin_0, LDR.pin_0
  N2: XIAO_RP2040.D1, R3.Pin_0
  N3: XIAO_RP2040.D2, R4.Pin_0
  N4: XIAO_RP2040.D3, R5.Pin_0
  N5: XIAO_RP2040.D4, DSP_OLED.SDA
  N6: XIAO_RP2040.D5, DSP_OLED.SCL
  N7: XIAO_RP2040.D6, R6.Pin_0
  N8: XIAO_RP2040.D7, R7.Pin_0
  N9: XIAO_RP2040.D8, R8.Pin_0
  N10: XIAO_RP2040.D9, R9.Pin_0
  N11: XIAO_RP2040.D10, R10.Pin_0
  N12: XIAO_RP2040.3V3, R1.Pin_1
  GND: XIAO_RP2040.GND, LDR.pin_1, PWR_5V.pin2, IC1.ADJ, DSP_OLED.GND, C1.1, C2.0, LEDCPU.pin1, LEDFAN2.pin1, ICUE1.pin1, LEDFAN1.pin1, LEDFAN3.pin1, LEDEXTRA.pin1, LEDAIO.pin1, ICUE2.pin1
  N13: XIAO_RP2040.5V, D1.cathode, ICUE1.pin4
  N14: D1.anode, PWR_5V.pin1, IC1.IN, C1.0, LEDCPU.pin4, LEDFAN2.pin4, LEDFAN1.pin4, LEDFAN3.pin4, LEDEXTRA.pin4, LEDAIO.pin4, ICUE2.pin4
  N15: R3.Pin_1, LEDFAN3.pin3
  N16: R4.Pin_1, LEDFAN2.pin3
  N17: R5.Pin_1, LEDFAN1.pin3
  N18: R6.Pin_1, ICUE1.pin3
  N19: R7.Pin_1, ICUE2.pin3
  N20: R8.Pin_1, LEDAIO.pin3
  N21: R9.Pin_1, LEDCPU.pin3
  N22: R10.Pin_1, LEDEXTRA.pin3
  N23: IC1.OUT, DSP_OLED.VCC, C2.1, part.pad

notes:
  +
  -

custom parts:
  seeeduino-xiao: Seeeduino XIAO processor board.
  OLED Mono 0.56 inch blue or white: OLED, I2C 3.3V - 5V Blue and White text versions
